# Fritzing sketch OldArduiPhoneBasic (saved by Fritzing 0.9.3b)
breadboards: 1

parts:
  Part1 = Arduino Uno (Rev3) - ICSP
  U1 = Sharp PC817 [package=THT]
  R1 = Resistor [tolerance=±5% resistance=10k package="1206 [SMD]"]
  R2 = Resistor [tolerance=±5% resistance=10k package="1206 [SMD]"]
  R3 = Resistor [tolerance=±5% resistance=1k package="1206 [SMD]"]

nets:
  N1: Part1.GND, U1.Pin_2, R1.Pin_0, R2.Pin_1
  N2: Part1.D2, R1.Pin_1
  N3: Part1.D3_PWM, R2.Pin_0
  N4: Part1.D4, R3.Pin_1
  N5: U1.Pin_1, R3.Pin_0
